// Logisim project main.circ as structural Verilog: 1 circuit, main circuit main
module main (
);

  RAM #(.addrWidth(12)) ram_1 ();  // open: addr, data, sel, clk, ld, clr

  // Notes on the sheet:
  //   ВЫСОТА(36)
  //   ШИРИНА(76)
  //   12 бит адрес
  //   2736 СИМВОЛОВ ВСЕГО
endmodule
